// Digital circuit Latihan Aldi diagram.dig as structural Verilog
module Latihan_Aldi_diagram (
  input  A,
  input  _1,
  input  A_2,
  input  _1_2,
  input  A_3,
  input  A_4,
  input  A_5,
  input  A_6,
  input  A_7,
  input  A_8,
  input  A_9,
  input  A_10,
  output X,
  output X_2,
  output X_3,
  output X_4,
  output X_5,
  output X_6
);

  wire not_1_out, not_2_out;

  and and_1 (X_2, A_2, _1_2);
  and and_2 (X_4, A_5, A_6);
  or or_1 (X, A, _1);
  or or_2 (X_3, A_3, A_4);
  or or_3 (X_5, A_7, not_1_out);
  not not_1 (not_1_out, A_8);
  and and_3 (X_6, A_9, not_2_out);
  not not_2 (not_2_out, A_10);

  // Notes on the sheet:
  //   A.A=A
  //   A.1=1
  //   Latihan Aldi  Diagram
  //   A+1=1
  //   A+A=A
  //   A+A'=1
  //   A+A'=0
endmodule
