// Digital circuit UAS1.10.dig as structural Verilog
module UAS1_10 (
  input  W,
  input  X,
  input  Y,
  input  Z,
  output A
);

  wire and_1_out, and_2_out, and_3_out, and_4_out, not_1_out, not_2_out, not_3_out;

  not not_1 (not_1_out, X);
  not not_2 (not_2_out, Z);
  and and_1 (and_1_out, W, not_1_out);
  not not_3 (not_3_out, W);
  and and_2 (and_2_out, W, X, Y, Z);
  and and_3 (and_3_out, W, not_1_out, Y);
  and and_4 (and_4_out, not_3_out, Y, not_2_out);
  or or_1 (A, and_2_out, and_1_out, and_3_out, and_4_out);

  // Notes on the sheet:
  //   WXYZ + WX' + WX'Y + WXY + W'YZ'
  //   Aldi Hermawan
endmodule
