// Digital circuit UAS1.11.dig as structural Verilog
module UAS1_11 (
  input  X,
  input  Y,
  input  Z,
  output A
);

  wire and_1_out, and_2_out, and_3_out, and_4_out, not_1_out, not_2_out, not_3_out, not_4_out, not_5_out;

  not not_1 (not_1_out, X);
  not not_2 (not_2_out, Y);
  not not_3 (not_3_out, Z);
  not not_4 (not_4_out, Z);
  not not_5 (not_5_out, X);
  and and_1 (and_1_out, not_1_out, not_2_out, not_3_out);
  and and_2 (and_2_out, X, Y, not_4_out);
  and and_3 (and_3_out, not_5_out, X, Y);
  and and_4 (and_4_out, X, Y);
  or or_1 (A, and_1_out, and_2_out, and_3_out, and_4_out);

  // Notes on the sheet:
  //   x'y'z' + xyz' + x' yz +xy
  //   Aldi Hermawan
endmodule
