// Digital circuit UAS1.5.dig as structural Verilog
module UAS1_5 (
  input  A,
  input  B,
  input  C,
  input  D,
  output X
);

  wire and_1_out, and_2_out, and_3_out, and_4_out, not_1_out, not_2_out, not_3_out, not_4_out, not_5_out;

  not not_1 (not_1_out, D);
  not not_2 (not_2_out, A);
  not not_3 (not_3_out, B);
  not not_4 (not_4_out, D);
  and and_1 (and_1_out, not_2_out, not_3_out, not_1_out);
  and and_2 (and_2_out, A, D);
  and and_3 (and_3_out, B, B, D);
  and and_4 (and_4_out, not_5_out, not_4_out);
  not not_5 (not_5_out, B);
  or or_1 (X, and_1_out, and_2_out, and_3_out, and_4_out);

  assign C = B;

  // Notes on the sheet:
  //   A'B'D' + A'D + BCD + BC' D'
  //   Aldi hermawan
endmodule
