// Digital circuit UAS1.6.dig as structural Verilog
module UAS1_6 (
  input  A,
  input  B,
  input  C,
  input  D,
  output X
);

  wire and_1_out, and_2_out, and_3_out, not_1_out, not_2_out, not_3_out, not_4_out, not_5_out, not_6_out,
       not_7_out;

  not not_1 (not_1_out, A);
  not not_2 (not_2_out, A);
  not not_3 (not_3_out, A);
  not not_4 (not_4_out, A);
  not not_5 (not_5_out, A);
  not not_6 (not_6_out, A);
  not not_7 (not_7_out, A);
  and and_1 (and_1_out, not_1_out, not_2_out, not_3_out);
  and and_2 (and_2_out, not_4_out, not_5_out, not_6_out);
  and and_3 (and_3_out, not_7_out, A, A);
  or or_1 (X, and_1_out, and_2_out, and_3_out);

  assign B = A;
  assign C = A;
  assign D = A;

  // Notes on the sheet:
  //   A'B'C' + A'C'D' + A'BC +ABD
  //   Aldi hermawan
endmodule
