// Digital circuit UAS1.9.dig as structural Verilog
module UAS1_9 (
  input  A,
  input  B,
  input  C,
  input  D,
  output X
);

  wire and_1_out, and_2_out, and_3_out, and_4_out, and_5_out, not_1_out, not_2_out, not_3_out, not_4_out;

  not not_1 (not_1_out, B);
  not not_2 (not_2_out, C);
  not not_3 (not_3_out, D);
  and and_1 (and_1_out, A, not_1_out, not_2_out);
  and and_2 (and_2_out, A, not_2_out, not_3_out);
  not not_4 (not_4_out, A);
  and and_3 (and_3_out, B, not_2_out, D);
  and and_4 (and_4_out, not_4_out, B, not_2_out, D);
  and and_5 (and_5_out, A, B, D);
  or or_1 (X, and_1_out, and_2_out, and_5_out, and_3_out, and_4_out);

  // Notes on the sheet:
  //   AB'C'+ AC'D'+ABD+BC'D+A'BC'D
  //   Aldi Hermawan
endmodule
