// Digital circuit Uas1.2.dig as structural Verilog
module Uas1_2 (
  input  A,
  input  B,
  input  C,
  input  D,
  output x
);

  wire and_1_out, and_2_out, and_3_out, and_4_out, and_5_out, not_1_out, not_2_out, not_3_out, not_4_out,
       not_5_out;

  not not_1 (not_1_out, A);
  not not_2 (not_2_out, B);
  not not_3 (not_3_out, C);
  not not_4 (not_4_out, D);
  not not_5 (not_5_out, C);
  and and_1 (and_1_out, not_1_out, not_2_out, not_3_out);
  and and_2 (and_2_out, not_1_out, C, D);
  and and_3 (and_3_out, not_1_out, not_3_out, not_4_out);
  and and_4 (and_4_out, not_1_out, B, D);
  and and_5 (and_5_out, A, B, not_5_out);
  or or_1 (x, and_1_out, and_2_out, and_3_out, and_4_out, and_5_out);

  // Notes on the sheet:
  //   A'B'C'  + A'CD + A'C'D' +A'BD+ABC +AB'C
  //   Aldi hermawan
endmodule
