// Digital circuit uas 1.1 digital.dig as structural Verilog
module uas_1_1_digital (
  input  B,
  input  A,
  input  C,
  output x
);

  wire and_1_out, not_1_out, or_1_out;

  or or_1 (or_1_out, A, A);
  not not_1 (not_1_out, or_1_out);
  and and_1 (and_1_out, not_1_out, A);
  or or_2 (x, and_1_out, A);

  assign B = A;
  assign C = A;

  // Notes on the sheet:
  //   Rangkaian Digital minggu 1
  //   UTS
endmodule
